# Fritzing sketch fritzing-diagram (saved by Fritzing 0.9.5d)
breadboards: 2

parts:
  2x16_LCD_display = LCD-16X2 [package=lcd-16x2]
  DHT11 = DHT11 Humitidy and Temperature Sensor
  LED1 = smd LED [color="Blue (430nm)" package="0805 [SMD]"]
  LED2 = smd LED [color="Red (633nm)" package="0805 [SMD]"]
  LED3 = smd LED [color="Yellow (595nm)" package="0805 [SMD]"]
  LED4 = smd LED [color="Green (555nm)" package="0805 [SMD]"]
  Start_(INT2) = Pushbutton [package="[THT]"]
  Reset_(INT4) = Pushbutton [package="[THT]"]
  Stop_(INT3) = Pushbutton [package="[THT]"]
  Stepper_motor = Adafruit Gear-Reduced Stepper Motor (small)
  ULN2003_stepper_motor_driver_board = 28BYJ-48 Driver Module [part_number=ULN2003 package=THT]
  Real_time_clock_module = Adafruit PCF8523 RTC [part_number=DS1307]
  Water_level_sensor = Water Level Sensor
  Vent_direction_pot = Trimmer Potentiometer [maximum_resistance=10kΩ package=THT]
  3-6v_DC_motor = DC Motor
  Arduino_Mega2560 = Arduino Mega 2560 (Rev3)
  R3 = Resistor [tolerance=±5% resistance=330 package=THT]
  R4 = Resistor [tolerance=±5% resistance=330 package=THT]
  R5 = Resistor [tolerance=±5% resistance=330 package=THT]
  R6 = Resistor [tolerance=±5% resistance=330 package=THT]
  R7 = Resistor [tolerance=±5% resistance=330 package=THT]
  LCD_pot = Trimmer Potentiometer [maximum_resistance=10kΩ package=THT]
  Q1 = NPN-Transistor [package="TO92 [THT]"]
  D1 = Rectifier Diode [part_number=1N4001 package="300 mil [THT]"]
  R8 = Resistor [tolerance=±5% resistance=330 package=THT]
  R9 = Resistor [tolerance=±5% resistance=330 package=THT]
  R10 = Resistor [tolerance=±5% resistance=330 package=THT]
  R11 = Resistor [tolerance=±5% resistance=330 package=THT]

nets:
  GND: 2x16_LCD_display.VSS, 2x16_LCD_display.R_W, 2x16_LCD_display.K, DHT11.GND, LED1.cathode, LED2.cathode, LED3.cathode, LED4.cathode, ULN2003_stepper_motor_driver_board.GND, Real_time_clock_module.GND, Water_level_sensor.GND, Vent_direction_pot.leg1, Arduino_Mega2560.GND, LCD_pot.leg1, Q1.E, R9.Pin_1, R10.Pin_1, R11.Pin_1
  VDD: 2x16_LCD_display.VDD, DHT11.VDD, Start_(INT2).Pin_3, Start_(INT2).Pin_4, Reset_(INT4).Pin_3, Reset_(INT4).Pin_4, Stop_(INT3).Pin_3, Stop_(INT3).Pin_4, ULN2003_stepper_motor_driver_board.Vmotor, Real_time_clock_module.VCC, Water_level_sensor.VCC, Vent_direction_pot.leg2, 3-6v_DC_motor.pin_2, Arduino_Mega2560.5V, R7.Pin_0, LCD_pot.leg2, D1.cathode
  N1: 2x16_LCD_display.VO, LCD_pot.wiper
  N2: 2x16_LCD_display.RS, Arduino_Mega2560.D8_PWM
  N3: 2x16_LCD_display.E, Arduino_Mega2560.D9_PWM
  N4: 2x16_LCD_display.DB4, Arduino_Mega2560.D10_PWM
  N5: 2x16_LCD_display.DB5, Arduino_Mega2560.D11_PWM
  N6: 2x16_LCD_display.DB6, Arduino_Mega2560.D12_PWM
  N7: 2x16_LCD_display.DB7, Arduino_Mega2560.D13_PWM
  N8: 2x16_LCD_display.A, R7.Pin_1
  N9: DHT11.DATA, Arduino_Mega2560.D50
  N10: LED1.anode, R6.Pin_1
  N11: LED2.anode, R3.Pin_1
  N12: LED3.anode, R4.Pin_1
  N13: LED4.anode, R5.Pin_1
  N14: Start_(INT2).Pin_1, Start_(INT2).Pin_2, Arduino_Mega2560.D19/RX1, R11.Pin_0
  N15: Reset_(INT4).Pin_1, Reset_(INT4).Pin_2, Arduino_Mega2560.D2_PWM, R9.Pin_0
  N16: Stop_(INT3).Pin_1, Stop_(INT3).Pin_2, Arduino_Mega2560.D18/TX1, R10.Pin_0
  N17: Stepper_motor.RED, ULN2003_stepper_motor_driver_board.blue-pin
  N18: Stepper_motor.ORANGE, ULN2003_stepper_motor_driver_board.pink-pin
  N19: Stepper_motor.YELLOW, ULN2003_stepper_motor_driver_board.yellow-pin
  N20: Stepper_motor.PINK, ULN2003_stepper_motor_driver_board.orange-pin
  N21: Stepper_motor.BLUE, ULN2003_stepper_motor_driver_board.red-pin
  N22: ULN2003_stepper_motor_driver_board.IN1, Arduino_Mega2560.D38
  N23: ULN2003_stepper_motor_driver_board.IN2, Arduino_Mega2560.D40
  N24: ULN2003_stepper_motor_driver_board.IN3, Arduino_Mega2560.D42
  N25: ULN2003_stepper_motor_driver_board.IN4, Arduino_Mega2560.D44
  N26: Real_time_clock_module.SCL, Arduino_Mega2560.D21/SCL
  N27: Real_time_clock_module.SDA, Arduino_Mega2560.D20/SDA
  N28: Water_level_sensor.SIG, Arduino_Mega2560.A1
  N29: Vent_direction_pot.wiper, Arduino_Mega2560.A0
  N30: 3-6v_DC_motor.pin_1, Q1.C, D1.anode
  N31: Arduino_Mega2560.D22, R6.Pin_0
  N32: Arduino_Mega2560.D24, R5.Pin_0
  N33: Arduino_Mega2560.D26, R4.Pin_0
  N34: Arduino_Mega2560.D28, R3.Pin_0
  N35: Arduino_Mega2560.D52, R8.Pin_0
  N36: Q1.B, R8.Pin_1

notes:
  Red = 5V
  Black = GND
  Yellow = Data out
  Blue = Digital data in
  Green = Analog (data) in
  White = special/fixed

custom parts:
  DHT11 Humitidy and Temperature Sensor: DHT11 Humidity and Temperature Sensor
  Adafruit Gear-Reduced Stepper Motor (small): Adafruit gear-reduction stepper motor (small)
  28BYJ-48 Driver Module: Generic male header
  Adafruit PCF8523 RTC: This is a great battery-backed real time clock (RTC) that allows your microcontroller project to keep track of time even if it is reprogrammed, or if the power is lost. Perfect for datalogging, clock-building, time stamping, timers and alarms, etc. Equipped with PCF8523 RTC - it can run from 3.3V or 5V power & logic! Works great with an Arduino using our RTC library, with CircuitPython or with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
  Water Level Sensor: A water level sensor. This sensor operates at 3V to 5V. The Sig (signal) pin outputs an analogue signal that is in proportion to the amount of water in contact with the sensor.
